# Fritzing sketch borne_avancee (saved by Fritzing 0.9.3b)
breadboards: 1

parts:
  Composant1 = Arduino Uno (Rev3) - ICSP
  U1 = LCD-16X2 [package=lcd-16x2]
  Matrix_keypad2 = KEYPAD 4x4
  LCM1602_IIC2 = LCM1602 IIC [part_number="LCM1602 IIC" chip_label="LCM1602 IIC" package="DIP (Dual Inline) [THT]"]
  Componente2 = RFID-RC522-v2
  LED1 = LED - 3mm [color="Red (633nm)" package="3 mm [THT]"]
  J1 = Piezo Speaker
  R1 = Resistor [tolerance=±5% resistance=220 package=THT]
  Part3 = ENC28J60 Breakout Board

nets:
  N1: Composant1.A0, Matrix_keypad2.col4
  N2: Composant1.A1, Matrix_keypad2.col3
  N3: Composant1.A2, Matrix_keypad2.col2
  N4: Composant1.A3, Matrix_keypad2.col1
  N5: Composant1.A4/SDA, LCM1602_IIC2.SDA
  N6: Composant1.A5/SCL, LCM1602_IIC2.SCL
  N7: Composant1.D8, Part3.CS
  N8: Composant1.D9_PWM, Componente2.RST
  N9: Composant1.D10_PWM/SS, Componente2.SDA
  N10: Composant1.D11_PWM/MOSI, Componente2.MOSI
  N11: Composant1.D12/MISO, Componente2.MISO
  N12: Composant1.D13/SCK, Componente2.SCK
  GND: Composant1.GND, LCM1602_IIC2.GND, Componente2.GND, J1.pin1
  N13: Composant1.D2, Part3.INT
  N14: Composant1.D3_PWM, LED1.anode
  N15: Composant1.D4, Matrix_keypad2.row4
  N16: Composant1.D5_PWM, Matrix_keypad2.row3
  N17: Composant1.D6_PWM, Matrix_keypad2.row2
  N18: Composant1.D7, Matrix_keypad2.row1
  N19: Composant1.RESET, Part3.RESET
  3V3: Composant1.3V3, Componente2.3.3V
  5V: Composant1.5V, LCM1602_IIC2.VCC
  VSS: U1.VSS, LCM1602_IIC2.VSS
  VDD: U1.VDD, LCM1602_IIC2.VDD
  N20: U1.VO, LCM1602_IIC2.V0
  N21: U1.RS, LCM1602_IIC2.RS
  N22: U1.R_W, LCM1602_IIC2.RW
  N23: U1.E, LCM1602_IIC2.E
  N24: U1.DB0, LCM1602_IIC2.D0
  N25: U1.DB1, LCM1602_IIC2.D1
  N26: U1.DB2, LCM1602_IIC2.D2
  N27: U1.DB3, LCM1602_IIC2.D3
  N28: U1.DB4, LCM1602_IIC2.D4
  N29: U1.DB5, LCM1602_IIC2.D5
  N30: U1.DB6, LCM1602_IIC2.D6
  N31: U1.DB7, LCM1602_IIC2.D7
  N32: U1.A, LCM1602_IIC2.A
  N33: U1.K, LCM1602_IIC2.K
  N34: LCM1602_IIC2.LED_A, LCM1602_IIC2.LED_B
  N35: LED1.cathode, R1.Pin_0
  N36: J1.pin2, R1.Pin_1

custom parts:
  KEYPAD 4x4: Matrix keypad 16 buttons, 4 rows x 4 columns
  LCM1602 IIC: I2C-Module to use a 1602 or 2004 LCD on with the wire.h libory Serial LCD Modul
  RFID-RC522-v2: A simple China made RFID-RC522 Reader; do check the pin labels, as this is a MFRC522 based clone.
  ENC28J60 Breakout Board: This is a breakout board for the Microchip ENC28J60 stand-alone ethernet controller. The ENC28J60 has an SPI interface. It operates at 3.3 Volts.
