# Fritzing sketch Borne_classique (saved by Fritzing 0.9.3b)

parts:
  Componente3 = RFID-RC522-v2
  Composant1 = Arduino Nano (Rev3.0)
  J1 = Piezo Speaker
  LED1 = smd LED [color="Red (633nm)" package="1206 [SMD]"]
  R1 = Resistor [tolerance=±5% resistance=220 package="1206 [SMD]"]  # not connected
  Part5 = ENC28J60 Breakout Board

nets:
  N1: Componente3.SDA, Composant1.D10
  N2: Componente3.SCK, Composant1.D13/SCK
  N3: Componente3.MOSI, Composant1.D11/MOSI
  N4: Componente3.MISO, Composant1.D12/MISO
  GND: Componente3.GND, Composant1.GND, J1.pin1
  N5: Componente3.RST, Composant1.D9
  3.3V: Componente3.3.3V, Composant1.3V3
  N6: Composant1.D2, Part5.INT
  N7: Composant1.D3, LED1.anode
  N8: Composant1.D8, Part5.CS
  N9: Composant1.RESET, Part5.RESET

custom parts:
  RFID-RC522-v2: A simple China made RFID-RC522 Reader; do check the pin labels, as this is a MFRC522 based clone.
  ENC28J60 Breakout Board: This is a breakout board for the Microchip ENC28J60 stand-alone ethernet controller. The ENC28J60 has an SPI interface. It operates at 3.3 Volts.
